# Fritzing sketch bbb-over-ftdi (saved by Fritzing 0.9.6b)

parts:
  BeagleBone1 = BeagleBone Black
  Part1 = Adafruit FTDI Friend [part_number="Adafruit #284"]

nets:
  N1: BeagleBone1.no_name_yet#201, Part1.GND
  N2: BeagleBone1.no_name_yet#204, Part1.TX
  N3: BeagleBone1.no_name_yet#205, Part1.RX

notes:
  FTDI GND <-> PIN1
  FTDI TX <-> PIN4
  FTDI RX <-> PIN5
  FTDI Voltage: 3.3V

custom parts:
  BeagleBone Black: BeagleBone Black rev. A5B
  Adafruit FTDI Friend: Long gone are the days of parallel ports and serial ports. Now the USB port reigns supreme! But USB is hard, and you just want to transfer your every-day serial data from a microcontroller to computer. What now? Enter the FTDI Friend! The FTDI Friend is a tweaked out FTDI FT232RL chip adapter. Sure, like the well-known FTDI cable, it can provide power to your project and there are 4 signal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
